# Fritzing sketch circuit (saved by Fritzing 0.9.3b)
breadboards: 1

parts:
  Part1 = Arduino MKR1000
  LED1 = RGB LED (com. cathode, rgb) [package="5 mm [THT]"]
  LCD1 = LCD screen
  RE1 = Rotary Encoder [package=THT]
  T1 = LM35 Temperature Sensor [package="TO92 [THT]"]
  R1 = Resistor [tolerance=±5% resistance=220 package=THT]  # not connected
  U1 = LIPO-1000mAh [package=lipo-1000]  # not connected

nets:
  N1: Part1.A1, T1.Vout
  N2: Part1.A4, LED1.red_anode
  N3: Part1.A5, LED1.common_cathode
  N4: Part1.A6, LED1.blue_anode
  N5: Part1.D6, LCD1.DB4
  N6: Part1.D7, LCD1.DB5
  N7: Part1.D8_MOSI, LCD1.DB6
  N8: Part1.D9_SCK, LCD1.DB7
  N9: Part1.D11_SDA, LCD1.E
  N10: Part1.D12_SCL, LCD1.RS
  GND: Part1.GND, LCD1.VSS, LCD1.R/W, LCD1.LED-
  5V: Part1.5V, LCD1.VDD, LCD1.LED+
  N11: LED1.green_anode, RE1.EncoderPinA, T1.GND
  N12: LCD1.V0, RE1.EncoderPinC
  N13: RE1.EncoderPinB, T1.+Vs

custom parts:
  Arduino MKR1000: MKR1000 is a powerful board that combines the functionality of the Zero and the Wi-Fi Shield. It is the ideal solution for makers wanting to design IoT projects with minimal previous experience in networking
